# Fritzing sketch Arduino_揚聲器(喇叭)連接電路圖 (saved by Fritzing 0.9.2b)
breadboards: 1

parts:
  元件1 = Arduino Uno (Rev3)
  SP1 = SPEAKER [package=pcb_mount_speaker]

nets:
  N1: 元件1.D7, SP1.-
  N2: 元件1.5V, SP1.+
