# Fritzing sketch Arduino_發光二極體連接電路圖 (saved by Fritzing 0.9.2b)
breadboards: 1

parts:
  元件1 = Arduino Uno (Rev3)
  LED1 = LED - 3mm [color="Red (633nm)" package="3 mm [THT]"]
  R1 = Resistor [tolerance=±5% resistance=220 package=THT]

nets:
  N1: 元件1.D13/SCK, R1.Pin_0
  N2: 元件1.GND, LED1.cathode
  N3: LED1.anode, R1.Pin_1
