# Fritzing sketch Arduino_舵機連接電路圖 (saved by Fritzing 0.9.2b)
breadboards: 1

parts:
  J1 = Basic Servo
  J2 = Basic Servo
  元件1 = Arduino Uno (Rev3)

nets:
  GND: J1.gnd, J2.gnd, 元件1.GND
  VCC: J1.vcc, J2.vcc, 元件1.5V
  N1: J1.pulse, 元件1.D11_PWM/MOSI
  N2: J2.pulse, 元件1.D12/MISO

notes:
  [SERVO 1]
  pin D11
  [SERVO 1]
  pin D12
