# Fritzing sketch Arduino基本電路_Blink(PWD_D8) (saved by Fritzing 0.9.2b)
breadboards: 1

parts:
  元件1 = Arduino Mega 2560 (Rev3)
  R4 = Resistor [tolerance=±5% resistance=220 package=THT]
  LED5 = LED - 5mm [color="Red (633nm)" package="5 mm [THT]"]

nets:
  N1: 元件1.D8_PWM, R4.Pin_1
  N2: 元件1.GND, LED5.anode
  N3: R4.Pin_0, LED5.cathode
