# Fritzing sketch Arduino基本電路_L298N (saved by Fritzing 0.9.2b)
breadboards: 1

parts:
  元件1 = Arduino Uno (Rev3)
  M1 = DC Motor
  M2 = DC Motor
  S2 = H-Bridge with L298N [part_number=L298N]
  VCC1 = 4 x AAA Battery Mount

nets:
  N1: 元件1.D4, S2.IN4
  N2: 元件1.D5_PWM, S2.IN3
  N3: 元件1.D6_PWM, S2.IN2
  N4: 元件1.D7, S2.IN1
  5V: 元件1.5V, S2.5V
  GND: 元件1.GND, S2.GND
  N5: M1.pin_1, S2.OUT1-Motor1
  N6: M1.pin_2, S2.OUT2-Motor1
  N7: M2.pin_1, S2.OUT4-Motor2
  N8: M2.pin_2, S2.OUT3-Motor2
  N9: S2.12V, VCC1.+

custom parts:
  H-Bridge with L298N: h-bridge
