# Fritzing sketch ESP8266-A6 (saved by Fritzing 0.9.3b)
breadboards: 1

parts:
  A6_Module_Ver3 = IC, DIP package, 24 pins [chip_label="A6 GSM"]
  WeMos_D1_Mini1 = WeMos D1 Mini
  R1 = Resistor [tolerance=±5% resistance=2.2k package=THT]
  R2 = Resistor [tolerance=±5% resistance=2.2k package=THT]
  2N2222 = NPN-Transistor [package="TO92 [THT]"]
  2N2222_2 = NPN-Transistor [package="TO92 [THT]"]
  R3 = Resistor [tolerance=±5% resistance=220 package=THT]
  R4 = Resistor [tolerance=±5% resistance=220 package=THT]
  S1 = SPST Switch [package=switch-spst-smd-a]

nets:
  N1: A6_Module_Ver3.pin1, WeMos_D1_Mini1.5V, 2N2222_2.C, S1.S
  GND: A6_Module_Ver3.pin2, WeMos_D1_Mini1.G, R1.Pin_1, R2.Pin_1, 2N2222.E
  N2: A6_Module_Ver3.pin8, WeMos_D1_Mini1.D2
  N3: A6_Module_Ver3.pin9, WeMos_D1_Mini1.D1
  N4: A6_Module_Ver3.pin13, 2N2222_2.E
  N5: A6_Module_Ver3.pin19, 2N2222.C
  N6: WeMos_D1_Mini1.D7, R4.Pin_0
  N7: WeMos_D1_Mini1.D8, R3.Pin_0
  N8: R1.Pin_0, 2N2222_2.B, R3.Pin_1
  N9: R2.Pin_0, 2N2222.B, R4.Pin_1
  5V: S1.P

// code stored in the sketch: GS_A6_Test1.ino
// Communication between ESP8266 and A6 Module Ver.3
// I am using the Wemos D1 Mini as ESP8266 module, but others works too.
//
// Created by Kjell Lindstrom, 2016-11-12
// Free to use for anyone

#include <SoftwareSerial.h>
SoftwareSerial mySerial(4,5); //4 = D2 on the MCU and 5 = D1 on MCU (Rx and Tx)


void setup() {
Serial.begin(115200); //This is the communication to the Serial Monitor
mySerial.begin(115200); // This is the communication between the MCU and the A6

pinMode(13, OUTPUT); // D7 (13) to power a 2N2222 transistor to reset the A6
pinMode(15, OUTPUT); // D8 (15) to power a 2N2222 transistor enable the A6 for some seconds on start.
digitalWrite(13, LOW); //Default settings for D7 (13)
digitalWrite(15, HIGH); // Default settings for D8 (15)

//Reset A6 so it initiates
digitalWrite(13, HIGH);
delay(1000);
digitalWrite(13, LOW);


// After delay, remove power from the enable pin on the A6
delay(3000);
digitalWrite(15, LOW);
}

void loop() {
// Here you can do whatever you want with the ESP8266 and A6. The A6 is using AT commands.

//I have just some code to test the A6 where I read the output from A6 and reads answers to Serial.  
if (mySerial.available()) {
  Serial.write(mySerial.read());

}
if (Serial.available()){
  mySerial.write(Serial.read());
//End of my communication code  


}
}
