# Fritzing sketch Progetto PIR con accensione LED (saved by Fritzing 0.9.1b)
breadboards: 1

parts:
  Raspberry_Pi1 = Raspberry Pi B+
  PIR1 = PIR sensor
  LED2 = smd LED [color="Red (633nm)" package="1206 [SMD]"]

nets:
  N1: Raspberry_Pi1.GPIO17, PIR1.SIG
  GND: Raspberry_Pi1.GND, PIR1.GND, LED2.anode
  N2: Raspberry_Pi1.GPIO18, LED2.cathode
  5V: Raspberry_Pi1.5V, PIR1.VDD

// code stored in the sketch: Untitled2.bas
import RPi.GPIO as GPIO
import time
pir=11
led=12
GPIO.setmode(GPIO.BOARD)
GPIO.setup(pir,GPIO.IN)
GPIO.setup(led,GPIO.OUT)
while 1:
			if GPIO.input(pir):
	
						GPIO.output (led,GPIO.HIGH)
						print "Ti Vedo!"
						time.sleep (5)
			else:
			
						GPIO.output (led,GPIO.LOW)
						print "Non ti vedo"
						time.sleep (1)
