# Fritzing sketch Shift_Register (saved by Fritzing 0.4.3b)
breadboards: 2

parts:
  74HC5951 = 74HC595 [package="DIP16 [THT]"]
  Arduino1 = Arduino
  R2 = Resistor [resistance=220 package=THT]
  R3 = Resistor [resistance=220 package=THT]
  R4 = Resistor [resistance=220 package=THT]
  R5 = Resistor [resistance=220 package=THT]
  R6 = Resistor [resistance=220 package=THT]
  R7 = Resistor [resistance=220 package=THT]
  R8 = Resistor [resistance=220 package=THT]
  R9 = Resistor [resistance=220 package=THT]
  LED2 = Red LED - 5mm
  LED3 = Red LED - 5mm
  LED4 = Red LED - 5mm
  LED5 = Red LED - 5mm
  LED6 = Red LED - 5mm
  LED7 = Red LED - 5mm
  LED8 = Red LED - 5mm
  LED9 = Red LED - 5mm
  C2 = Ceramic Capacitor [package=THT]

nets:
  N1: 74HC5951.Q1, R5.Pin_1
  N2: 74HC5951.Q2, R6.Pin_1
  N3: 74HC5951.Q3, R7.Pin_1
  N4: 74HC5951.Q4, R9.Pin_1
  N5: 74HC5951.Q5, R2.Pin_1
  N6: 74HC5951.Q6, R3.Pin_1
  N7: 74HC5951.Q7, R8.Pin_1
  GND: 74HC5951.GND, 74HC5951.OE, Arduino1.GND, LED2.cathode, LED3.cathode, LED4.cathode, LED5.cathode, LED6.cathode, LED7.cathode, LED8.cathode, LED9.cathode, C2.pin_1
  VCC: 74HC5951.MR, 74HC5951.VCC, Arduino1.+5V
  N8: 74HC5951.SH_CP, Arduino1.D12
  N9: 74HC5951.ST_CP, Arduino1.D8, C2.pin_0
  N10: 74HC5951.DS, Arduino1.D11
  N11: 74HC5951.Q0, R4.Pin_1
  N12: R2.Pin_0, LED6.anode
  N13: R3.Pin_0, LED8.anode
  N14: R4.Pin_0, LED9.anode
  N15: R5.Pin_0, LED4.anode
  N16: R6.Pin_0, LED2.anode
  N17: R7.Pin_0, LED5.anode
  N18: R8.Pin_0, LED7.anode
  N19: R9.Pin_0, LED3.anode

notes:
  In this project, a 74HC595 shift register is used to control 8 LEDs with just 3 Arduino pins.
  Related example: http://www.arduino.cc/en/Tutorial/ShiftOut
  [write your note here]
