# Fritzing sketch TbStepperDriver (saved by Fritzing 0.7.1b)
breadboards: 1

parts:
  TB1 = TB6560
  R1 = Resistor [tolerance=±5% resistance=4.7k package=THT]
  R2 = Resistor [tolerance=±5% resistance=4.7k package=THT]
  C1 = Ceramic Capacitor [capacitance=1µF package="100 mil [THT, multilayer]"]
  C2 = Ceramic Capacitor [capacitance=0.1µF package="100 mil [THT, multilayer]"]
  Power_plug2 = Power plug
  Arduino1 = Arduino Mega
  J1 = male pin header, 4 pins [form="♂ (male)"]
  C5 = Electrolytic Capacitor [capacitance=10µF voltage=16V package="100 mil [THT, electrolytic]"]
  C6 = Electrolytic Capacitor [capacitance=10µF voltage=16V package="100 mil [THT, electrolytic]"]
  C7 = Ceramic Capacitor [capacitance=1µF voltage=16V package="100 mil [THT, multilayer]"]

nets:
  N1: TB1.Noch_kein_Name#0, TB1.Noch_kein_Name#1, TB1.Noch_kein_Name#4, TB1.Noch_kein_Name#19, TB1.Noch_kein_Name#21, TB1.Noch_kein_Name#22, C1.0, Arduino1.+5V, C6.+
  N2: TB1.Noch_kein_Name#2, Arduino1.D26
  N3: TB1.Noch_kein_Name#3, Arduino1.D24
  GND: TB1.Noch_kein_Name#5, TB1.Noch_kein_Name#9, TB1.Noch_kein_Name#14, R1.Pin_1, R2.Pin_1, C1.1, C2.0, Power_plug2.GND, Arduino1.GND, C5.-, C6.-, C7.0
  N4: TB1.Noch_kein_Name#6, C2.1
  N5: TB1.Noch_kein_Name#7, TB1.Noch_kein_Name#17, Power_plug2.VCC, C5.+, C7.1
  N6: TB1.Noch_kein_Name#8, J1.pin4
  N7: TB1.Noch_kein_Name#10, R2.Pin_0
  N8: TB1.Noch_kein_Name#11, J1.pin3
  N9: TB1.Noch_kein_Name#12, J1.pin2
  N10: TB1.Noch_kein_Name#13, R1.Pin_0
  N11: TB1.Noch_kein_Name#15, J1.pin1
  N12: TB1.Noch_kein_Name#20, Arduino1.D28
