# Fritzing sketch max7219 (saved by Fritzing 0.7.0b)
breadboards: 1

parts:
  MAX_7219 = MAX 7219 [package="DIP (Dual Inline) [THT]"]
  100nF = Ceramic Capacitor [capacitance=100nF package="100 mil [THT, multilayer]"]
  VCC/GND = female pin header, 2 pins [form="♀ (female)"]
  LOAD/CLK = female pin header, 2 pins [form="♀ (female)"]
  DIN/DOUT = female pin header, 2 pins [form="♀ (female)"]
  7_SEG/ANODEN_0 = female pin header, 8 pins [form="♀ (female)"]
  0_DIG/KATHODEN_7 = female pin header, 8 pins [form="♀ (female)"]
  LOAD/CLK_2 = female pin header, 2 pins [form="♀ (female)"]
  ISET = Resistor [tolerance=±5% resistance=220 package=THT]
  10uF = Electrolytic Capacitor [capacitance=10µF package="100 mil [THT, electrolytic]"]

nets:
  N1: MAX_7219.DIN, DIN/DOUT.pin1
  N2: MAX_7219.DIG_0, 0_DIG/KATHODEN_7.pin8
  N3: MAX_7219.DIG_4, 0_DIG/KATHODEN_7.pin4
  N4: MAX_7219.GND, 100nF.1, VCC/GND.pin2, 10uF.-
  N5: MAX_7219.DIG_6, 0_DIG/KATHODEN_7.pin2
  N6: MAX_7219.DIG_2, 0_DIG/KATHODEN_7.pin6
  N7: MAX_7219.DIG_3, 0_DIG/KATHODEN_7.pin5
  N8: MAX_7219.DIG_7, 0_DIG/KATHODEN_7.pin1
  N9: MAX_7219.DIG_5, 0_DIG/KATHODEN_7.pin3
  N10: MAX_7219.DIG_1, 0_DIG/KATHODEN_7.pin7
  N11: MAX_7219.LOAD_(CS), LOAD/CLK.pin1, LOAD/CLK_2.pin1
  N12: MAX_7219.CLK, LOAD/CLK.pin2, LOAD/CLK_2.pin2
  N13: MAX_7219.SEG_A, 7_SEG/ANODEN_0.pin2
  N14: MAX_7219.SEG_F, 7_SEG/ANODEN_0.pin7
  N15: MAX_7219.SEG_B, 7_SEG/ANODEN_0.pin3
  N16: MAX_7219.SEG_G, 7_SEG/ANODEN_0.pin8
  N17: MAX_7219.ISET, ISET.Pin_1
  N18: MAX_7219.V+, 100nF.0, VCC/GND.pin1, ISET.Pin_0, 10uF.+
  N19: MAX_7219.SEG_C, 7_SEG/ANODEN_0.pin4
  N20: MAX_7219.SEG_E, 7_SEG/ANODEN_0.pin6
  N21: MAX_7219.SEG_DP, 7_SEG/ANODEN_0.pin1
  N22: MAX_7219.SEG_D, 7_SEG/ANODEN_0.pin5
  N23: MAX_7219.DOUT, DIN/DOUT.pin2

custom parts:
  MAX 7219: A led matrix driver on a 300 mil dual inline package (DIP) footprint.
